# Fritzing sketch d1_buisness_card_pcb (saved by Fritzing 0.9.3b)
circuit board: 3.00159cm x 3.40402cm
circuit board: 3.00159cm x 3.40402cm
circuit board: 2.76076cm x 2.38049cm
breadboards: 1

parts:
  WeMos_D1_Mini1 = WeMos D1 Mini  # not connected
  J1 = female pin header, 8 pins [form="♀ (female)"]
  J2 = female pin header, 8 pins [form="♀ (female)"]
  RHT1 = Humidity and Temperature Sensor RHT03
  JP1 = Header 2 [package=jst-2-pth]
  U1 = Voltage Regulator - 5V [package="TO220 [THT]"]
  J3 = female pin header, 8 pins [form="♀ (female)"]  # not connected
  J4 = female pin header, 8 pins [form="♀ (female)"]  # not connected
  J7 = female pin header, 8 pins [form="♀ (female)"]
  J8 = female pin header, 8 pins [form="♀ (female)"]
  Squix4 = OLED 0.96" 128x64 I2C SSD1306

nets:
  N1: J1.pin7, RHT1.GND_2, JP1.1, U1.GND
  N2: J1.pin8, U1.output_voltage
  N3: J2.pin7, RHT1.Data-signal
  N4: J2.pin8, RHT1.Vcc
  N5: JP1.2, U1.input_voltage
  N6: J7.pin3, Squix4.SCL
  N7: J7.pin4, Squix4.SCA
  N8: J7.pin7, Squix4.GND
  N9: J8.pin8, Squix4.VCC

notes:
  OLED I2C
  DHT22 +
  5v D1 Mini
