# Fritzing sketch d1_oled_shield_pcb (saved by Fritzing 0.9.3b)
circuit board: 2.76076cm x 2.38049cm
breadboards: 1

parts:
  J5 = female pin header, 8 pins [form="♀ (female)"]
  J6 = female pin header, 8 pins [form="♀ (female)"]
  Squix3 = OLED 0.96" 128x64 I2C SSD1306
  WeMos_D1_Mini3 = WeMos D1 Mini  # not connected

nets:
  N1: J5.pin3, Squix3.SCL
  N2: J5.pin4, Squix3.SCA
  N3: J5.pin7, Squix3.GND
  N4: J6.pin8, Squix3.VCC

notes:
  OLED I2C
