# Fritzing sketch d1_shield_pcb (saved by Fritzing 0.9.3b)
circuit board: 2.84378cm x 3.21836cm
circuit board: 3.00159cm x 3.40402cm
breadboards: 1

parts:
  WeMos_D1_Mini1 = WeMos D1 Mini  # not connected
  J1 = female pin header, 8 pins [form="♀ (female)"]
  J2 = female pin header, 8 pins [form="♀ (female)"]
  RHT1 = Humidity and Temperature Sensor RHT03
  JP1 = Header 2 [package=jst-2-pth]
  U1 = Voltage Regulator - 5V [package="TO220 [THT]"]
  J3 = female pin header, 8 pins [form="♀ (female)"]  # not connected
  J4 = female pin header, 8 pins [form="♀ (female)"]  # not connected

nets:
  N1: J1.pin7, RHT1.GND_2, JP1.1, U1.GND
  N2: J1.pin8, U1.output_voltage
  N3: J2.pin7, RHT1.Data-signal
  N4: J2.pin8, RHT1.Vcc
  N5: JP1.2, U1.input_voltage

notes:
  DHT22 +
  5v D1 Mini
  GND
  7+V
