# Fritzing sketch nodemcu_shield_base (saved by Fritzing 0.9.3b)
circuit board: 2.66858cm x 4.4119cm
breadboards: 1

parts:
  J4 = male pin header, 2 pins [form="♂ (male)"]
  J5 = male pin header, 15 pins [form="♂ (male)"]  # not connected
  J6 = male pin header, 15 pins [form="♂ (male)"]
  IC2 = Voltage Regulator [package=to220-igo]
  U2 = NodeMCU V1.0  # not connected

nets:
  N1: J4.pin1, IC2.IN
  N2: J4.pin2, J6.pin14, IC2.GND
  N3: J6.pin15, IC2.OUT

notes:
  A0
  G10
  G09
  MOSI
  CS
  MISO
  SCLK
  GND
  3V3
  EN
  RST
  Vin
  D0
  D1
  D3
  D4
  D5
  D6
  D7
  D8
  D9
  D10
  D2

custom parts:
  NodeMCU V1.0: ESP8266 based NodeMCU
