# Fritzing sketch nodemcu_led_strip_mosfet_shield (saved by Fritzing 0.9.3b)
circuit board: 4.68646cm x 4.58122cm
breadboards: 1

parts:
  U2 = NodeMCU V1.0  # not connected
  Q1 = Basic FET N-Channel [package="TO220 [THT]"]
  Q2 = Basic FET N-Channel [package="TO220 [THT]"]
  Q3 = Basic FET N-Channel [package="TO220 [THT]"]
  J4 = male pin header, 2 pins [form="♂ (male)"]
  J5 = male pin header, 15 pins [form="♂ (male)"]
  J6 = male pin header, 15 pins [form="♂ (male)"]
  IC2 = Voltage Regulator [package=to220-igo]
  J7 = male pin header, 4 pins [form="♂ (male)"]

nets:
  N1: Q1.gate, J5.pin2
  N2: Q1.drain, J7.pin3
  N3: Q1.source, Q2.source, Q3.source, J4.pin2, J5.pin14, IC2.GND
  N4: Q2.gate, J5.pin3
  N5: Q2.drain, J7.pin2
  N6: Q3.gate, J5.pin4
  N7: Q3.drain, J7.pin1
  N8: J4.pin1, IC2.IN, J7.pin4
  N9: J6.pin15, IC2.OUT

notes:
  G
  D
  S
  D2
  MOSI
  RX/D7
  TX/D10
  EN
  GND
  3V3
  D0
  MISO
  D6
  SCLK
  D3
  TX/D4
  G09
  RX/D9
  HSCLK/D5
  G10
  Vin
  D8
  CS
  RST
  D1
  A0
  +12V
  R
  B

custom parts:
  NodeMCU V1.0: ESP8266 based NodeMCU
