# Fritzing sketch nodemcu_oled_weather_clock (saved by Fritzing 0.9.3b)
circuit board: 2.95079cm x 4.94811cm
breadboards: 1

parts:
  U1 = NodeMCU V1.0  # not connected
  J1 = male pin header, 15 pins [form="♂ (male)"]
  J2 = male pin header, 15 pins [form="♂ (male)"]
  Squix1 = OLED 0.96" 128x64 I2C SSD1306
  IC1 = Voltage Regulator [package=to220-igo]
  J3 = male pin header, 2 pins [form="♂ (male)"]
  DHT1 = DHT22 Humidity and Temperature Sensor

nets:
  N1: J1.pin14, IC1.GND, J3.pin2
  N2: J1.pin15, IC1.OUT
  N3: J2.pin6, Squix1.VCC
  N4: J2.pin7, Squix1.GND
  N5: J2.pin8, Squix1.SCA
  N6: J2.pin9, DHT1.NULL
  N7: J2.pin11, Squix1.SCL
  N8: J2.pin14, DHT1.DATA
  N9: J2.pin15, DHT1.VDD
  N10: IC1.IN, J3.pin1

notes:
  3V GND SCL SCA
  A0
  G10
  G09
  GND
  D3
  TX/D10
  SCLK
  HSCLK/D5
  MISO
  RX/D9
  Vin
  D2
  CS
  3V3
  D1
  D8
  D6
  RX/D7
  EN
  TX/D4
  RST
  D0
  MOSI

custom parts:
  NodeMCU V1.0: ESP8266 based NodeMCU
